// Logisim project Lab1Bonus.circ as structural Verilog: 1 circuit, main circuit main
module main (
);

  wire and_1_out, and_2_out, button_1_out, button_2_out, nand_1_out, nor_1_out, not_1_out, or_1_out,
       or_2_out, or_3_out, Test_Helper_q0, Test_Helper_q1, Test_Helper_q2, xnor_1_out, xnor_2_out;

  Button button_1 (.out(button_1_out));
  Button button_2 (.out(button_2_out));
  Lab1TestHelper Test_Helper (
    .T(button_1_out), .Q2(Test_Helper_q2), .Q1(Test_Helper_q1), .Q0(Test_Helper_q0), .R(button_2_out));
  LED C (.in(Test_Helper_q0));
  LED B (.in(Test_Helper_q1));
  LED A (.in(Test_Helper_q2));
  // Probe on Test_Helper_q2
  // Probe on Test_Helper_q1
  // Probe on Test_Helper_q0
  or or_1 (or_1_out, Test_Helper_q1, Test_Helper_q0);
  and and_1 (and_1_out, Test_Helper_q0, Test_Helper_q1);
  nand nand_1 (nand_1_out, Test_Helper_q2, Test_Helper_q1);
  nor nor_1 (nor_1_out, Test_Helper_q2, Test_Helper_q0);
  not not_1 (not_1_out, and_1_out);
  or or_2 (or_2_out, nand_1_out, ~Test_Helper_q1);  // OR_Gate
  and and_2 (and_2_out, or_1_out, not_1_out);
  or or_3 (or_3_out, Test_Helper_q2, and_2_out);
  NotExactlyOne xnor_1 (.out(xnor_1_out), .in0(or_2_out), .in1(Test_Helper_q1), .in2(nor_1_out));
  LED Y (.in(or_3_out));
  LED X (.in(xnor_1_out));
  xnor xnor_2 (xnor_2_out, xnor_1_out, or_3_out);
  LED Z (.in(xnor_2_out));

  // Notes on the sheet:
  //   A
  //   B
  //   C
  //   X
endmodule
