// Logisim project Lab1Mystery.circ as structural Verilog: 1 circuit, main circuit main
module main (
);

  wire button_1_out, button_2_out, nand_1_out, nor_1_out, or_1_out, Test_Helper_q0, Test_Helper_q1,
       Test_Helper_q2, undriven, undriven_2, undriven_3, xnor_1_out;

  Button button_1 (.out(button_1_out));
  Button button_2 (.out(button_2_out));
  Lab1TestHelper Test_Helper (
    .T(button_1_out), .Q2(Test_Helper_q2), .Q1(Test_Helper_q1), .Q0(Test_Helper_q0), .R(button_2_out));
  LED led_1 (.in(Test_Helper_q0));
  LED led_2 (.in(Test_Helper_q1));
  LED led_3 (.in(Test_Helper_q2));
  // Probe on Test_Helper_q2
  // Probe on Test_Helper_q1
  // Probe on Test_Helper_q0
  nand nand_1 (nand_1_out, undriven, undriven_2);
  nor nor_1 (nor_1_out, undriven, undriven_3);
  or or_1 (or_1_out, nand_1_out, undriven_2);
  NotExactlyOne xnor_1 (.out(xnor_1_out), .in0(or_1_out), .in1(undriven_2), .in2(nor_1_out));
  LED led_4 (.in(xnor_1_out));

  // Notes on the sheet:
  //   A
  //   B
  //   C
  //   X
endmodule
