// Logisim project Lab1Mystrey.circ as structural Verilog: 1 circuit, main circuit main
module main (
);

  wire button_1_out, button_2_out, lab1testhelper_1_q0, lab1testhelper_1_q1, lab1testhelper_1_q2;

  Button button_1 (.out(button_1_out));
  Button button_2 (.out(button_2_out));
  Lab1TestHelper lab1testhelper_1 (
    .T(button_1_out), .Q2(lab1testhelper_1_q2), .Q1(lab1testhelper_1_q1), .Q0(lab1testhelper_1_q0),
    .R(button_2_out));
  LED led_1 (.in(lab1testhelper_1_q0));
  LED led_2 (.in(lab1testhelper_1_q2));
  LED led_3 (.in(lab1testhelper_1_q1));
  // Probe on lab1testhelper_1_q2
  // Probe on lab1testhelper_1_q1
  // Probe on lab1testhelper_1_q0
endmodule
