// Logisim project Lab1StartDone.circ as structural Verilog: 1 circuit, main circuit main
module main (
);

  wire button_1_out, button_2_out, Test_Helper_q0, Test_Helper_q1, Test_Helper_q2;

  Button button_1 (.out(button_1_out));
  Button button_2 (.out(button_2_out));
  Lab1TestHelper Test_Helper (
    .T(button_1_out), .Q2(Test_Helper_q2), .Q1(Test_Helper_q1), .Q0(Test_Helper_q0), .R(button_2_out));
  LED led_1 (.in(Test_Helper_q0));
  LED led_2 (.in(Test_Helper_q1));
  LED led_3 (.in(Test_Helper_q2));
  // Probe on Test_Helper_q2
  // Probe on Test_Helper_q1
  // Probe on Test_Helper_q0
endmodule
