// Logisim project Lab1TestHelper.circ as structural Verilog: 1 circuit, main circuit Lab1TestHelper
module Lab1TestHelper (
  input  T,
  input  R,
  output Q2,
  output Q1,
  output Q0
);

  Counter #(.width(3), .max('h7)) counter_1 (.Q({Q2, Q1, Q0}), .clk(T), .clr(R));  // open: load, D, count, carry
endmodule
