// Logisim project Lab3Solution.circ as structural Verilog: 1 circuit, main circuit main
module main (
);

  wire adder_1_cout, and_1_out, and_2_out, and_3_out, and_4_out, button_1_out, button_2_out,
       lab3testhelper_1_done, nand_1_out, nor_1_out, not_2_out, or_1_out, xnor_1_out;
  wire [7:0] adder_1_out, lab3testhelper_1_x, lab3testhelper_1_y, not_1_out;

  Button button_1 (.out(button_1_out));
  Button button_2 (.out(button_2_out));
  LED Done (.in(lab3testhelper_1_done));
  Lab3TestHelper lab3testhelper_1 (
    .C(button_1_out), .X(lab3testhelper_1_x), .R(button_2_out), .Y(lab3testhelper_1_y),
    .Done(lab3testhelper_1_done));
  // Probe on lab3testhelper_1_y
  // Probe on lab3testhelper_1_y
  // Probe on lab3testhelper_1_y
  // Probe on lab3testhelper_1_x
  // Probe on lab3testhelper_1_x
  // Probe on lab3testhelper_1_x
  assign not_1_out = ~lab3testhelper_1_y;  // NOT_Gate not_1, 8 bits wide
  Adder adder_1 (.a(not_1_out), .b(lab3testhelper_1_x), .out(adder_1_out), .cin(1'b1), .cout(adder_1_cout));
  and and_1 (and_1_out, ~lab3testhelper_1_y[7], lab3testhelper_1_x[7]);  // AND_Gate
  // Probe on adder_1_out
  // Probe on adder_1_out
  // Probe on adder_1_out
  nand nand_1 (nand_1_out, ~lab3testhelper_1_y[7], lab3testhelper_1_x[7]);  // NAND_Gate
  not not_2 (not_2_out, adder_1_cout);
  and and_2 (and_2_out, ~adder_1_out[7], nand_1_out);  // AND_Gate
  nor nor_1 (nor_1_out, adder_1_out[0], adder_1_out[1], adder_1_out[2], adder_1_out[3], adder_1_out[4], adder_1_out[5], adder_1_out[6], adder_1_out[7]);
  xnor xnor_1 (xnor_1_out, nor_1_out, and_4_out);
  or or_1 (or_1_out, and_2_out, and_1_out);
  and and_3 (and_3_out, ~nor_1_out, adder_1_cout);  // AND_Gate
  and and_4 (and_4_out, ~nor_1_out, or_1_out);  // AND_Gate
  LED U (.in(nor_1_out));
  LED S (.in(nor_1_out));
  LED U_2 (.in(not_2_out));
  LED U_3 (.in(and_3_out));
  LED S_2 (.in(xnor_1_out));
  LED S_3 (.in(and_4_out));
endmodule
