// Logisim project Lab3Start.circ as structural Verilog: 1 circuit, main circuit main
module main (
);

  wire button_1_out, button_2_out, lab3testhelper_1_done;
  wire [7:0] lab3testhelper_1_x, lab3testhelper_1_y;

  Button button_1 (.out(button_1_out));
  Button button_2 (.out(button_2_out));
  LED Done (.in(lab3testhelper_1_done));
  Lab3TestHelper lab3testhelper_1 (
    .C(button_1_out), .X(lab3testhelper_1_x), .R(button_2_out), .Y(lab3testhelper_1_y),
    .Done(lab3testhelper_1_done));
  // Probe on lab3testhelper_1_y
  // Probe on lab3testhelper_1_y
  // Probe on lab3testhelper_1_y
  // Probe on lab3testhelper_1_x
  // Probe on lab3testhelper_1_x
  // Probe on lab3testhelper_1_x
endmodule
