// Logisim project Lab3TestHelper.circ as structural Verilog: 1 circuit, main circuit Lab3TestHelper
module Lab3TestHelper (
  input  C,
  input  R,
  output Done,
  output [7:0] Y,
  output [7:0] X
);

  wire and_1_out, comparator_1_gt;
  wire [2:0] counter_1_q;

  // Probe on counter_1_q
  Counter #(.width(3), .max('h7), .ongoal("stay")) counter_1 (
    .Q(counter_1_q), .clk(and_1_out), .clr(R));  // open: load, D, count, carry
  and and_1 (and_1_out, comparator_1_gt, C);
  not not_1 (Done, comparator_1_gt);
  Comparator #(.width(3), .mode("unsigned")) comparator_1 (
    .a(3'b111), .b(counter_1_q), .gt(comparator_1_gt));  // open: eq, lt
  ROM #(.addrWidth(3), .dataWidth(16)) rom_1 (.addr(counter_1_q), .data({X, Y}));  // open: sel

  // Notes on the sheet:
  //   contents of rom_1 (hex, n*v repeats v):
  //   102 8585 eaac 72f2 b925 25b9 ff
endmodule
