// Logisim project Lab4Reset.circ as structural Verilog: 1 circuit, main circuit main
module main (
);

  wire and_1_out, and_2_out, and_4_out, and_5_out, and_6_out, and_7_out, and_8_out, and_9_out, and_10_out,
       and_11_out, and_12_out, and_13_out, and_14_out, and_15_out, and_16_out, and_17_out, and_18_out,
       and_19_out, comparator_1_gt, comparator_2_lt, comparator_3_gt, comparator_4_lt, comparator_5_gt,
       comparator_6_lt, comparator_7_gt, comparator_8_lt, d_ff_1_q, d_ff_1_qn, d_ff_2_q, d_ff_2_qn, d_ff_3_q,
       d_ff_3_qn, decoder_1_out0, Keep_Going, nand_1_out, nand_2_out, Reset, Stuck, Ticker;
  wire [3:0] adder_1_out, adder_2_out, Ball_X, Ball_Y, Next_Ball_X, Next_Ball_Y, xor_1_out, xor_5_out;
  wire [14:0] decoder_1_out1, demultiplexer_1_out0, demultiplexer_1_out1, demultiplexer_1_out2,
       demultiplexer_1_out3, demultiplexer_1_out4, demultiplexer_1_out5, demultiplexer_1_out6,
       demultiplexer_1_out7, demultiplexer_1_out8, demultiplexer_1_out9, demultiplexer_1_out10,
       demultiplexer_1_out11, demultiplexer_1_out12, demultiplexer_1_out13, demultiplexer_1_out14,
       demultiplexer_1_out15;

  Clock clock_1 (.out(Ticker));
  Register #(.width(4)) Current_Ball_X_Position (
    .D(Next_Ball_X), .en(Keep_Going), .Q(Ball_X), .clk(Ticker));  // open: clr
  Register #(.width(4)) Current_Ball_Y_Position (
    .D(Next_Ball_Y), .en(Keep_Going), .Q(Ball_Y), .clk(Ticker));  // open: clr
  // Probe on Ball_X
  // Probe on Ball_Y
  Decoder #(.select(4), .enable("false")) decoder_1 (
    .out0(decoder_1_out0), .out1(decoder_1_out1[0]), .out2(decoder_1_out1[1]), .out3(decoder_1_out1[2]),
    .out4(decoder_1_out1[3]), .out5(decoder_1_out1[4]), .out6(decoder_1_out1[5]), .out7(decoder_1_out1[6]),
    .out8(decoder_1_out1[7]), .out9(decoder_1_out1[8]), .out10(decoder_1_out1[9]),
    .out11(decoder_1_out1[10]), .out12(decoder_1_out1[11]), .out13(decoder_1_out1[12]),
    .out14(decoder_1_out1[13]), .out15(decoder_1_out1[14]), .sel(Ball_Y));
  DotMatrix #(.matrixcols(14), .matrixrows(15)) dotmatrix_1 (
    .col0(demultiplexer_1_out1), .col1(demultiplexer_1_out2), .col2(demultiplexer_1_out3),
    .col3(demultiplexer_1_out4), .col4(demultiplexer_1_out5), .col5(demultiplexer_1_out6),
    .col6(demultiplexer_1_out7), .col7(demultiplexer_1_out8), .col8(demultiplexer_1_out9),
    .col9(demultiplexer_1_out10), .col10(demultiplexer_1_out11), .col11(demultiplexer_1_out12),
    .col12(demultiplexer_1_out13), .col13(demultiplexer_1_out14));
  Demultiplexer #(.select(4), .width(15), .enable("false")) demultiplexer_1 (
    .out0(demultiplexer_1_out0), .out1(demultiplexer_1_out1), .out2(demultiplexer_1_out2),
    .out3(demultiplexer_1_out3), .out4(demultiplexer_1_out4), .out5(demultiplexer_1_out5),
    .out6(demultiplexer_1_out6), .out7(demultiplexer_1_out7), .out8(demultiplexer_1_out8),
    .out9(demultiplexer_1_out9), .out10(demultiplexer_1_out10), .out11(demultiplexer_1_out11),
    .out12(demultiplexer_1_out12), .out13(demultiplexer_1_out13), .out14(demultiplexer_1_out14),
    .out15(demultiplexer_1_out15), .in(decoder_1_out1), .sel(Ball_X));
  Button button_1 (.out(Reset));
  LED led_1 (.in(Stuck));
  LED led_2 (.in(1'b0));
  Comparator #(.width(4), .mode("unsigned")) comparator_1 (
    .a(Ball_X), .b(4'b0001), .gt(comparator_1_gt));  // open: eq, lt
  Comparator #(.width(4), .mode("unsigned")) comparator_2 (
    .a(Ball_X), .b(4'b1110), .lt(comparator_2_lt));  // open: gt, eq
  Comparator #(.width(4), .mode("unsigned")) comparator_3 (
    .a(Ball_Y), .b(4'b0001), .gt(comparator_3_gt));  // open: eq, lt
  Comparator #(.width(4), .mode("unsigned")) comparator_4 (
    .a(Ball_Y), .b(4'b1110), .lt(comparator_4_lt));  // open: gt, eq
  Comparator #(.width(4), .mode("unsigned")) comparator_5 (
    .a(Ball_X), .b(4'b0100), .gt(comparator_5_gt));  // open: eq, lt
  Comparator #(.width(4), .mode("unsigned")) comparator_6 (
    .a(Ball_X), .b(4'b1100), .lt(comparator_6_lt));  // open: gt, eq
  Comparator #(.width(4), .mode("unsigned")) comparator_7 (
    .a(Ball_Y), .b(4'b0100), .gt(comparator_7_gt));  // open: eq, lt
  Comparator #(.width(4), .mode("unsigned")) comparator_8 (
    .a(Ball_Y), .b(4'b1100), .lt(comparator_8_lt));  // open: gt, eq
  nand nand_1 (nand_1_out, comparator_1_gt, comparator_2_lt);
  nand nand_2 (nand_2_out, comparator_3_gt, comparator_4_lt);
  and and_1 (and_1_out, comparator_5_gt, comparator_6_lt);
  and and_2 (and_2_out, comparator_7_gt, comparator_8_lt);
  D_Flip_Flop d_ff_1 (
    .clk(nand_1_out), .D(d_ff_1_qn), .Q(d_ff_1_q), .Qn(d_ff_1_qn), .en(Keep_Going));  // open: preset, reset
  D_Flip_Flop d_ff_2 (
    .clk(nand_2_out), .D(d_ff_2_qn), .Q(d_ff_2_q), .Qn(d_ff_2_qn), .en(Keep_Going));  // open: preset, reset
  and and_3 (Stuck, and_1_out, and_2_out);
  Adder #(.width(4)) adder_1 (.a(Ball_X), .b(xor_1_out), .out(adder_1_out), .cin(d_ff_1_q));  // open: cout
  Adder #(.width(4)) adder_2 (.a(Ball_Y), .b(xor_5_out), .out(adder_2_out), .cin(d_ff_2_q));  // open: cout
  D_Flip_Flop d_ff_3 (.clk(Ticker), .D(d_ff_3_qn), .Q(d_ff_3_q), .Qn(d_ff_3_qn));  // open: preset, en, reset
  xor xor_1 (xor_1_out[0], 1'b1, d_ff_1_q);
  xor xor_2 (xor_1_out[1], 1'b0, d_ff_1_q);
  xor xor_3 (xor_1_out[2], 1'b0, d_ff_1_q);
  xor xor_4 (xor_1_out[3], 1'b0, d_ff_1_q);
  xor xor_5 (xor_5_out[0], 1'b1, d_ff_2_q);
  xor xor_6 (xor_5_out[1], 1'b0, d_ff_2_q);
  xor xor_7 (xor_5_out[2], 1'b0, d_ff_2_q);
  xor xor_8 (xor_5_out[3], 1'b0, d_ff_2_q);
  nand nand_3 (Keep_Going, d_ff_3_q, Stuck);
  and and_4 (and_4_out, ~Reset, adder_1_out[0]);  // AND_Gate
  and and_5 (and_5_out, Reset, 1'b1);
  and and_6 (and_6_out, ~Reset, adder_1_out[1]);  // AND_Gate
  and and_7 (and_7_out, Reset, 1'b0);
  and and_8 (and_8_out, ~Reset, adder_1_out[2]);  // AND_Gate
  and and_9 (and_9_out, Reset, 1'b0);
  and and_10 (and_10_out, ~Reset, adder_1_out[3]);  // AND_Gate
  and and_11 (and_11_out, Reset, 1'b0);
  and and_12 (and_12_out, ~Reset, adder_2_out[0]);  // AND_Gate
  and and_13 (and_13_out, Reset, 1'b1);
  and and_14 (and_14_out, ~Reset, adder_2_out[1]);  // AND_Gate
  and and_15 (and_15_out, Reset, 1'b1);
  and and_16 (and_16_out, ~Reset, adder_2_out[2]);  // AND_Gate
  and and_17 (and_17_out, Reset, 1'b1);
  and and_18 (and_18_out, ~Reset, adder_2_out[3]);  // AND_Gate
  and and_19 (and_19_out, Reset, 1'b0);
  or or_1 (Next_Ball_X[0], and_4_out, and_5_out);
  or or_2 (Next_Ball_X[1], and_6_out, and_7_out);
  or or_3 (Next_Ball_X[2], and_8_out, and_9_out);
  or or_4 (Next_Ball_X[3], and_10_out, and_11_out);
  or or_5 (Next_Ball_Y[0], and_12_out, and_13_out);
  or or_6 (Next_Ball_Y[1], and_14_out, and_15_out);
  or or_7 (Next_Ball_Y[2], and_16_out, and_17_out);
  or or_8 (Next_Ball_Y[3], and_18_out, and_19_out);

  // Notes on the sheet:
  //   Ball Y Decoder
  //   14 (X) x 15 (Y) LED Matrix
  //   (1,1) in lower left corner
endmodule
