// Logisim project Lab4X.circ as structural Verilog: 1 circuit, main circuit main
module main (
);

  wire comparator_1_eq, comparator_2_eq, decoder_1_out0, Reset, Ticker;
  wire [3:0] Ball_X, Ball_Y, Next_Ball_X, Next_Ball_Y, xor_1_out;
  wire [3:3] d_ff_1_q;
  wire [14:0] decoder_1_out1, demultiplexer_1_out0, demultiplexer_1_out1, demultiplexer_1_out2,
       demultiplexer_1_out3, demultiplexer_1_out4, demultiplexer_1_out5, demultiplexer_1_out6,
       demultiplexer_1_out7, demultiplexer_1_out8, demultiplexer_1_out9, demultiplexer_1_out10,
       demultiplexer_1_out11, demultiplexer_1_out12, demultiplexer_1_out13, demultiplexer_1_out14,
       demultiplexer_1_out15;

  Clock clock_1 (.out(Ticker));
  Register #(.width(4)) Current_Ball_X_Position (.D(Next_Ball_X), .en(1'b1), .Q(Ball_X), .clk(Ticker));  // open: clr
  Register #(.width(4)) Current_Ball_Y_Position (.D(Next_Ball_Y), .en(1'b1), .Q(Ball_Y), .clk(Ticker));  // open: clr
  // Probe on Ball_X
  // Probe on Ball_Y
  Decoder #(.select(4), .enable("false")) decoder_1 (
    .out0(decoder_1_out0), .out1(decoder_1_out1[0]), .out2(decoder_1_out1[1]), .out3(decoder_1_out1[2]),
    .out4(decoder_1_out1[3]), .out5(decoder_1_out1[4]), .out6(decoder_1_out1[5]), .out7(decoder_1_out1[6]),
    .out8(decoder_1_out1[7]), .out9(decoder_1_out1[8]), .out10(decoder_1_out1[9]),
    .out11(decoder_1_out1[10]), .out12(decoder_1_out1[11]), .out13(decoder_1_out1[12]),
    .out14(decoder_1_out1[13]), .out15(decoder_1_out1[14]), .sel(Ball_Y));
  DotMatrix #(.matrixcols(14), .matrixrows(15)) dotmatrix_1 (
    .col0(demultiplexer_1_out1), .col1(demultiplexer_1_out2), .col2(demultiplexer_1_out3),
    .col3(demultiplexer_1_out4), .col4(demultiplexer_1_out5), .col5(demultiplexer_1_out6),
    .col6(demultiplexer_1_out7), .col7(demultiplexer_1_out8), .col8(demultiplexer_1_out9),
    .col9(demultiplexer_1_out10), .col10(demultiplexer_1_out11), .col11(demultiplexer_1_out12),
    .col12(demultiplexer_1_out13), .col13(demultiplexer_1_out14));
  Demultiplexer #(.select(4), .width(15), .enable("false")) demultiplexer_1 (
    .out0(demultiplexer_1_out0), .out1(demultiplexer_1_out1), .out2(demultiplexer_1_out2),
    .out3(demultiplexer_1_out3), .out4(demultiplexer_1_out4), .out5(demultiplexer_1_out5),
    .out6(demultiplexer_1_out6), .out7(demultiplexer_1_out7), .out8(demultiplexer_1_out8),
    .out9(demultiplexer_1_out9), .out10(demultiplexer_1_out10), .out11(demultiplexer_1_out11),
    .out12(demultiplexer_1_out12), .out13(demultiplexer_1_out13), .out14(demultiplexer_1_out14),
    .out15(demultiplexer_1_out15), .in(decoder_1_out1), .sel(Ball_X));
  Button button_1 (.out(Reset));
  LED led_1 (.in(1'b0));
  LED led_2 (.in(1'b0));
  Comparator #(.width(4), .mode("unsigned")) comparator_1 (
    .a(Ball_X), .b(4'b0001), .eq(comparator_1_eq));  // open: gt, lt
  Comparator #(.width(4), .mode("unsigned")) comparator_2 (
    .a(Ball_X), .b(4'b1110), .eq(comparator_2_eq));  // open: gt, lt
  D_Flip_Flop d_ff_1 (.Q(d_ff_1_q[3]), .preset(comparator_2_eq), .reset(comparator_1_eq));  // open: clk, D, Qn, en
  assign xor_1_out = {4{d_ff_1_q[3]}} ^ 4'b0001;  // XOR_Gate xor_1, 4 bits wide
  Adder #(.width(4)) adder_1 (.a(xor_1_out), .b(Ball_X), .out(Next_Ball_X), .cin(d_ff_1_q[3]));  // open: cout

  // Notes on the sheet:
  //   Ball Y Decoder
  //   14 (X) x 15 (Y) LED Matrix
  //   (1,1) in lower left corner
endmodule
