// Logisim project Lab5_bonus.circ as structural Verilog: 1 circuit, main circuit main
module main (
);

  wire _4_Way_Off, _4_Way_On, Brake_Off, Brake_On, Left_Turn_q, Left_Turn_qn, No_Turn, Right_Turn_q,
       Right_Turn_qn, Tick, Turn_Left, Turn_Right;
  wire [2:0] Left, Left_Lights, register_1_q, register_2_q, register_3_q, Right, Right_Lights, rom_1_data,
       rom_2_data, rom_3_data, rom_4_data;

  D_Flip_Flop Left_Turn (.Q(Left_Turn_q), .Qn(Left_Turn_qn));  // open: clk, D, preset, en, reset
  LED led_1 (.in(Left_Lights[0]));
  LED led_2 (.in(Left_Lights[1]));
  LED led_3 (.in(Left_Lights[2]));
  and and_1 (Turn_Left, Left_Turn_q, Right_Turn_qn);
  xnor xnor_1 (No_Turn, Left_Turn_q, Right_Turn_q);
  LED led_4 (.in(Right_Lights[1]));
  LED led_5 (.in(Right_Lights[2]));
  D_Flip_Flop Right_Turn (.Q(Right_Turn_q), .Qn(Right_Turn_qn));  // open: clk, D, preset, en, reset
  and and_2 (Turn_Right, Left_Turn_qn, Right_Turn_q);
  Clock clock_1 (.out(Tick));
  LED led_6 (.in(Right_Lights[0]));
  Register #(.width(3)) register_1 (.D(rom_1_data), .en(_4_Way_On), .Q(register_1_q), .clk(Tick), .clr(_4_Way_Off));
  D_Flip_Flop Brake (.Q(Brake_On), .Qn(Brake_Off));  // open: clk, D, preset, en, reset
  D_Flip_Flop _4_Way (.Q(_4_Way_On), .Qn(_4_Way_Off));  // open: clk, D, preset, en, reset
  ROM #(.addrWidth(3), .dataWidth(3)) rom_1 (.addr(register_1_q), .data(rom_1_data));  // open: sel
  Register #(.width(3)) register_2 (.D(rom_3_data), .en(Turn_Left), .Q(register_2_q), .clk(Tick), .clr(No_Turn));
  Register #(.width(3)) register_3 (.D(rom_4_data), .en(Turn_Right), .Q(register_3_q), .clk(Tick), .clr(No_Turn));
  ROM #(.addrWidth(3), .dataWidth(3)) rom_2 (.addr(rom_1_data), .data(rom_2_data));  // open: sel
  ROM #(.addrWidth(3), .dataWidth(3)) rom_3 (.addr(register_2_q), .data(rom_3_data));  // open: sel
  ROM #(.addrWidth(3), .dataWidth(3)) rom_4 (.addr(register_3_q), .data(rom_4_data));  // open: sel
  Multiplexer #(.select(3), .width(3)) multiplexer_1 (
    .in0(3'b000), .in1(Left), .in2(3'b111), .in3(Left), .in4(rom_2_data), .in5(rom_2_data), .in6(3'b111),
    .in7(3'b111), .out(Left_Lights), .sel({_4_Way_On, Brake_On, Turn_Left}));  // open: en
  Multiplexer #(.select(3), .width(3)) multiplexer_2 (
    .in0(3'b000), .in1(Right), .in2(3'b111), .in3(Right), .in4(rom_2_data), .in5(rom_2_data), .in6(3'b111),
    .in7(3'b111), .out(Right_Lights), .sel({_4_Way_On, Brake_On, Turn_Right}));  // open: en
  ROM #(.addrWidth(3), .dataWidth(3)) rom_5 (.addr(rom_4_data), .data(Right));  // open: sel
  ROM #(.addrWidth(3), .dataWidth(3)) rom_6 (.addr(rom_3_data), .data(Left));  // open: sel

  // Notes on the sheet:
  //   Left Turn Group
  //   Right Turn Group
  //   contents of rom_1 (hex, n*v repeats v):
  //   7
  //   contents of rom_2 (hex, n*v repeats v):
  //   7
  //   contents of rom_3 (hex, n*v repeats v):
  //   1 3 0 7
  //   contents of rom_4 (hex, n*v repeats v):
  //   4 0 0 0 6 0 7
  //   contents of rom_5 (hex, n*v repeats v):
  //   4 0 0 0 6 0 7
  //   contents of rom_6 (hex, n*v repeats v):
  //   1 3 0 7
endmodule
