// Logisim project Lab2Enigma1.circ as structural Verilog: 1 circuit, main circuit main
module main (
);

  wire and_1_out, and_2_out, button_1_out, button_2_out, lab1testhelper_1_q0, lab1testhelper_1_q1,
       lab1testhelper_1_q2, or_1_out, or_2_out, xor_1_out, xor_2_out;

  Button button_1 (.out(button_1_out));
  Button button_2 (.out(button_2_out));
  Lab1TestHelper lab1testhelper_1 (
    .T(button_1_out), .Q2(lab1testhelper_1_q2), .Q1(lab1testhelper_1_q1), .Q0(lab1testhelper_1_q0),
    .R(button_2_out));
  LED X (.in(lab1testhelper_1_q2));
  LED Y (.in(lab1testhelper_1_q1));
  LED Z (.in(lab1testhelper_1_q0));
  xor xor_1 (xor_1_out, lab1testhelper_1_q2, lab1testhelper_1_q1);
  xor xor_2 (xor_2_out, xor_1_out, lab1testhelper_1_q0);
  LED S (.in(xor_2_out));
  or or_1 (or_1_out, lab1testhelper_1_q1, lab1testhelper_1_q0);
  and and_1 (and_1_out, ~lab1testhelper_1_q2, or_1_out);  // AND_Gate
  and and_2 (and_2_out, lab1testhelper_1_q1, lab1testhelper_1_q0);
  or or_2 (or_2_out, and_1_out, and_2_out);
  LED R (.in(or_2_out));
endmodule
