// Logisim project Lab2Enigma8.circ as structural Verilog: 1 circuit, main circuit main
module main (
);

  wire and_1_out, and_2_out, and_3_out, and_4_out, and_5_out, and_6_out, and_7_out, and_8_out, and_9_out,
       and_10_out, and_11_out, and_12_out, and_13_out, and_14_out, and_15_out, and_16_out, or_1_out,
       or_2_out, or_3_out, or_4_out, or_5_out, or_6_out, or_7_out, or_8_out, or_9_out, or_10_out, or_11_out,
       or_12_out, or_13_out, or_14_out, or_15_out, or_16_out, xor_1_out, xor_3_out, xor_5_out, xor_7_out,
       xor_9_out, xor_11_out, xor_13_out, xor_15_out;
  wire [7:0] X_q, xor_16_out, Y_q;

  // Probe on X_q
  // Probe on X_q
  // Probe on X_q
  Register #(.trigger("falling")) X (.Q(X_q));  // open: D, en, clk, clr
  // Probe on xor_16_out
  // Probe on xor_16_out
  // Probe on xor_16_out
  xor xor_1 (xor_1_out, X_q[7], Y_q[7]);
  xor xor_2 (xor_16_out[7], xor_1_out, or_4_out);
  or or_1 (or_1_out, Y_q[7], or_4_out);
  and and_1 (and_1_out, ~X_q[7], or_1_out);  // AND_Gate
  and and_2 (and_2_out, Y_q[7], or_4_out);
  or or_2 (or_2_out, and_1_out, and_2_out);
  xor xor_3 (xor_3_out, X_q[6], Y_q[6]);
  xor xor_4 (xor_16_out[6], xor_3_out, or_6_out);
  or or_3 (or_3_out, Y_q[6], or_6_out);
  and and_3 (and_3_out, ~X_q[6], or_3_out);  // AND_Gate
  or or_4 (or_4_out, and_3_out, and_4_out);
  and and_4 (and_4_out, Y_q[6], or_6_out);
  xor xor_5 (xor_5_out, X_q[5], Y_q[5]);
  xor xor_6 (xor_16_out[5], xor_5_out, or_8_out);
  and and_5 (and_5_out, ~X_q[5], or_5_out);  // AND_Gate
  and and_6 (and_6_out, Y_q[5], or_8_out);
  or or_5 (or_5_out, Y_q[5], or_8_out);
  or or_6 (or_6_out, and_5_out, and_6_out);
  xor xor_7 (xor_7_out, X_q[4], Y_q[4]);
  xor xor_8 (xor_16_out[4], xor_7_out, or_10_out);
  or or_7 (or_7_out, Y_q[4], or_10_out);
  and and_7 (and_7_out, ~X_q[4], or_7_out);  // AND_Gate
  and and_8 (and_8_out, Y_q[4], or_10_out);
  or or_8 (or_8_out, and_7_out, and_8_out);
  xor xor_9 (xor_9_out, X_q[3], Y_q[3]);
  xor xor_10 (xor_16_out[3], xor_9_out, or_12_out);
  or or_9 (or_9_out, Y_q[3], or_12_out);
  and and_9 (and_9_out, ~X_q[3], or_9_out);  // AND_Gate
  or or_10 (or_10_out, and_9_out, and_10_out);
  and and_10 (and_10_out, Y_q[3], or_12_out);
  xor xor_11 (xor_11_out, X_q[2], Y_q[2]);
  xor xor_12 (xor_16_out[2], xor_11_out, or_14_out);
  or or_11 (or_11_out, Y_q[2], or_14_out);
  and and_11 (and_11_out, ~X_q[2], or_11_out);  // AND_Gate
  and and_12 (and_12_out, Y_q[2], or_14_out);
  or or_12 (or_12_out, and_11_out, and_12_out);
  xor xor_13 (xor_13_out, X_q[1], Y_q[1]);
  xor xor_14 (xor_16_out[1], xor_13_out, or_16_out);
  or or_13 (or_13_out, Y_q[1], or_16_out);
  and and_13 (and_13_out, ~X_q[1], or_13_out);  // AND_Gate
  and and_14 (and_14_out, Y_q[1], or_16_out);
  or or_14 (or_14_out, and_13_out, and_14_out);
  xor xor_15 (xor_15_out, X_q[0], Y_q[0]);
  xor xor_16 (xor_16_out[0], xor_15_out, 1'b0);
  or or_15 (or_15_out, Y_q[0], 1'b0);
  and and_15 (and_15_out, ~X_q[0], or_15_out);  // AND_Gate
  // Probe on Y_q
  // Probe on Y_q
  and and_16 (and_16_out, Y_q[0], 1'b0);
  or or_16 (or_16_out, and_15_out, and_16_out);
  // Probe on Y_q
  Register Y (.Q(Y_q));  // open: D, en, clk, clr
endmodule
