// Logisim project tryGuid.circ as structural Verilog: 1 circuit, main circuit main
module main (
);

  wire and_1_out, and_2_out, or_1_out;

  and and_1 (and_1_out, 1'b0, ~1'b1);  // AND_Gate
  and and_2 (and_2_out, ~1'b0, 1'b1);  // AND_Gate
  or or_1 (or_1_out, and_1_out, and_2_out);

  // Notes on the sheet:
  //   A
  //   B
  //   C
endmodule
